// Logisim project fase2-funciona-rex.circ as structural Verilog: 3 circuits, main circuit ALU
module REGs (
  input  [7:0] Rin,
  input  SEL,
  input  [7:0] Rex,
  input  rwCTL,
  input  CLEAR,
  input  [3:0] Rs1,
  input  CLK,
  input  [3:0] Rd,
  input  [3:0] Rs2,
  output R0,
  output [7:0] Rx,
  output [7:0] Ry
);

  wire and_1_out, demultiplexer_1_out0, demultiplexer_1_out1, demultiplexer_1_out2, demultiplexer_1_out3,
       demultiplexer_1_out4, demultiplexer_1_out5, demultiplexer_1_out6, demultiplexer_1_out7,
       demultiplexer_1_out8, demultiplexer_1_out9, demultiplexer_1_out10, demultiplexer_1_out11,
       demultiplexer_1_out12, demultiplexer_1_out13, demultiplexer_1_out14, demultiplexer_1_out15, not_1_out,
       or_1_out, or_2_out, or_3_out, or_4_out, or_5_out, or_6_out, or_7_out, or_8_out, or_9_out, or_10_out,
       or_11_out, or_12_out, or_13_out, or_14_out, or_15_out, or_16_out;
  wire [7:0] multiplexer_1_out, Reg0_q, Reg1_q, Reg2_q, Reg3_q, Reg4_q, Reg5_q, Reg6_q, Reg7_q, Reg8_q,
       Reg9_q, Reg10_q, Reg11_q, Reg12_q, Reg13_q, Reg14_q, Reg15_q;

  Demultiplexer #(.select(4), .enable("false")) demultiplexer_1 (
    .out0(demultiplexer_1_out0), .out1(demultiplexer_1_out1), .out2(demultiplexer_1_out2),
    .out3(demultiplexer_1_out3), .out4(demultiplexer_1_out4), .out5(demultiplexer_1_out5),
    .out6(demultiplexer_1_out6), .out7(demultiplexer_1_out7), .out8(demultiplexer_1_out8),
    .out9(demultiplexer_1_out9), .out10(demultiplexer_1_out10), .out11(demultiplexer_1_out11),
    .out12(demultiplexer_1_out12), .out13(demultiplexer_1_out13), .out14(demultiplexer_1_out14),
    .out15(demultiplexer_1_out15), .in(not_1_out), .sel(Rd));
  not not_1 (not_1_out, CLK);
  Multiplexer #(.width(8), .enable("false")) multiplexer_1 (.in0(Rin), .in1(Rex), .out(multiplexer_1_out), .sel(SEL));
  and and_1 (and_1_out, rwCTL, not_1_out);
  or or_1 (or_1_out, and_1_out, demultiplexer_1_out0);
  or or_2 (or_2_out, and_1_out, demultiplexer_1_out1);
  or or_3 (or_3_out, and_1_out, demultiplexer_1_out2);
  or or_4 (or_4_out, and_1_out, demultiplexer_1_out3);
  or or_5 (or_5_out, and_1_out, demultiplexer_1_out4);
  or or_6 (or_6_out, and_1_out, demultiplexer_1_out5);
  or or_7 (or_7_out, and_1_out, demultiplexer_1_out6);
  or or_8 (or_8_out, and_1_out, demultiplexer_1_out7);
  or or_9 (or_9_out, and_1_out, demultiplexer_1_out8);
  or or_10 (or_10_out, and_1_out, demultiplexer_1_out9);
  or or_11 (or_11_out, and_1_out, demultiplexer_1_out10);
  or or_12 (or_12_out, and_1_out, demultiplexer_1_out11);
  or or_13 (or_13_out, and_1_out, demultiplexer_1_out12);
  or or_14 (or_14_out, and_1_out, demultiplexer_1_out13);
  or or_15 (or_15_out, and_1_out, demultiplexer_1_out14);
  or or_16 (or_16_out, and_1_out, demultiplexer_1_out15);
  Register Reg0 (.D(multiplexer_1_out), .Q(Reg0_q), .clk(or_1_out), .clr(CLEAR));  // open: en
  Register Reg1 (.D(multiplexer_1_out), .Q(Reg1_q), .clk(or_2_out), .clr(CLEAR));  // open: en
  Register Reg2 (.D(multiplexer_1_out), .Q(Reg2_q), .clk(or_3_out), .clr(CLEAR));  // open: en
  Register Reg3 (.D(multiplexer_1_out), .Q(Reg3_q), .clk(or_4_out), .clr(CLEAR));  // open: en
  Register Reg4 (.D(multiplexer_1_out), .Q(Reg4_q), .clk(or_5_out), .clr(CLEAR));  // open: en
  Register Reg5 (.D(multiplexer_1_out), .Q(Reg5_q), .clk(or_6_out), .clr(CLEAR));  // open: en
  Register Reg6 (.D(multiplexer_1_out), .Q(Reg6_q), .clk(or_7_out), .clr(CLEAR));  // open: en
  Register Reg7 (.D(multiplexer_1_out), .Q(Reg7_q), .clk(or_8_out), .clr(CLEAR));  // open: en
  Register Reg8 (.D(multiplexer_1_out), .Q(Reg8_q), .clk(or_9_out), .clr(CLEAR));  // open: en
  Register Reg9 (.D(multiplexer_1_out), .Q(Reg9_q), .clk(or_10_out), .clr(CLEAR));  // open: en
  Register Reg10 (.D(multiplexer_1_out), .Q(Reg10_q), .clk(or_11_out), .clr(CLEAR));  // open: en
  Register Reg11 (.D(multiplexer_1_out), .Q(Reg11_q), .clk(or_12_out), .clr(CLEAR));  // open: en
  Register Reg12 (.D(multiplexer_1_out), .Q(Reg12_q), .clk(or_13_out), .clr(CLEAR));  // open: en
  Register Reg13 (.D(multiplexer_1_out), .Q(Reg13_q), .clk(or_14_out), .clr(CLEAR));  // open: en
  Register Reg14 (.D(multiplexer_1_out), .Q(Reg14_q), .clk(or_15_out), .clr(CLEAR));  // open: en
  Register Reg15 (.D(multiplexer_1_out), .Q(Reg15_q), .clk(or_16_out), .clr(CLEAR));  // open: en
  Multiplexer #(.select(4), .width(8), .enable("false")) multiplexer_2 (
    .in0(Reg0_q), .in1(Reg1_q), .in2(Reg2_q), .in3(Reg3_q), .in4(Reg4_q), .in5(Reg5_q), .in6(Reg6_q),
    .in7(Reg7_q), .in8(Reg8_q), .in9(Reg9_q), .in10(Reg10_q), .in11(Reg11_q), .in12(Reg12_q), .in13(Reg13_q),
    .in14(Reg14_q), .in15(Reg15_q), .out(Rx), .sel(Rs1));
  Multiplexer #(.select(4), .width(8), .enable("false")) multiplexer_3 (
    .in0(Reg0_q), .in1(Reg1_q), .in2(Reg2_q), .in3(Reg3_q), .in4(Reg4_q), .in5(Reg5_q), .in6(Reg6_q),
    .in7(Reg7_q), .in8(Reg8_q), .in9(Reg9_q), .in10(Reg10_q), .in11(Reg11_q), .in12(Reg12_q), .in13(Reg13_q),
    .in14(Reg14_q), .in15(Reg15_q), .out(Ry), .sel(Rs2));
  or or_17 (R0, Reg0_q[7], Reg0_q[6], Reg0_q[5], Reg0_q[4], Reg0_q[3], Reg0_q[2], Reg0_q[1], Reg0_q[0]);

  // Notes on the sheet:
  //   rwCTL: pull=up
endmodule

module ALU (
  input  [7:0] Ix,
  input  [7:0] Iy,
  input  [3:0] Op,
  output [7:0] Out
);

  wire comparator_1_eq, comparator_1_lt, not_1_out, NOT_Rx_out, or_2_out;
  wire [7:0] adder_1_out, AND_out, bit_extender_1_out, bitselector_1_out, bitselector_2_out,
       bitselector_3_out, divider_1_out, multiplier_1_out, OR_out, subtractor_1_out;

  assign AND_out = Ix & Iy;  // AND_Gate AND, 8 bits wide
  not not_1 (not_1_out, NOT_Rx_out);
  or NOT_Rx (NOT_Rx_out, Ix[0], Ix[1], Ix[2], Ix[3], Ix[4], Ix[5], Ix[6], Ix[7]);
  assign OR_out = Ix | Iy;  // OR_Gate OR, 8 bits wide
  Adder adder_1 (.a(Ix), .b(Iy), .out(adder_1_out));  // open: cin, cout
  Subtractor subtractor_1 (.a(Ix), .b(Iy), .out(subtractor_1_out));  // open: bin, bout
  Multiplier multiplier_1 (.a(Ix), .b(Iy), .out(multiplier_1_out));  // open: cin, cout
  Divider divider_1 (.a(Ix), .b(Iy), .out(divider_1_out));  // open: upper, rem
  Comparator #(.mode("unsigned")) comparator_1 (
    .a(Ix), .b(Iy), .eq(comparator_1_eq), .lt(comparator_1_lt));  // open: gt
  assign bit_extender_1_out = {{7{1'b0}}, not_1_out};  // Bit_Extender bit_extender_1
  or or_2 (or_2_out, comparator_1_eq, comparator_1_lt);
  Multiplexer #(.select(4), .width(8), .enable("false")) multiplexer_1 (
    .in0(AND_out), .in1(OR_out), .in2(bit_extender_1_out), .in3(adder_1_out), .in4(subtractor_1_out),
    .in5(multiplier_1_out), .in6(divider_1_out), .in7(bitselector_1_out), .in8(bitselector_3_out),
    .in9(bitselector_2_out), .out(Out), .sel(Op));  // open: in10, in11, in12, in13, in14, in15
  BitSelector #(.width(1), .group(8)) bitselector_1 (.in(comparator_1_eq), .out(bitselector_1_out), .sel(1'b0));
  BitSelector #(.width(1), .group(8)) bitselector_2 (.in(or_2_out), .out(bitselector_2_out), .sel(1'b0));
  LED LSB (.in(Out[0]));
  LED led_1 (.in(Out[1]));
  BitSelector #(.width(1), .group(8)) bitselector_3 (.in(comparator_1_lt), .out(bitselector_3_out), .sel(1'b0));
  LED led_2 (.in(Out[2]));
  LED led_3 (.in(Out[3]));
  LED led_4 (.in(Out[4]));
  LED led_5 (.in(Out[5]));
  LED led_6 (.in(Out[6]));
  LED MSB (.in(Out[7]));
  LED IGUAL (.in(comparator_1_eq));
  LED IGUAL_OU_MENOR (.in(or_2_out));
  LED MENOR (.in(comparator_1_lt));

  // Notes on the sheet:
  //   Ix: pull=up
endmodule

// REGs
module Principal (
  input  [3:0] in_1,
  input  [3:0] in_2,
  input  [3:0] in_3,
  input  [7:0] in_4,
  input  in_5,
  input  in_6,
  input  in_7,
  input  [3:0] in_8,
  output out_9,
  output [7:0] Ix,
  output [7:0] out_11,
  output [7:0] Iy
);

  wire CLK_out;

  Clock CLK (.out(CLK_out));
  REGs regs_1 (
    .Rin(in_4), .rwCTL(in_5), .Rs1(in_1), .Rd(in_3), .Rs2(in_2), .CLEAR(in_6), .Rx(Ix), .Ry(Iy), .R0(out_9),
    .CLK(CLK_out), .Rex(out_11), .SEL(in_7));
  ALU alu_1 (.Out(out_11), .Ix(Ix), .Iy(Iy), .Op(in_8));
endmodule
